// Logisim project Counter.circ as structural Verilog: 1 circuit, main circuit main
module main (
  input  in_1
);

  wire and_1_out, and_2_out, and_3_out, and_4_out, and_5_out, and_6_out, and_7_out, clock_1_out, j_k_ff_1_q,
       j_k_ff_1_qn, j_k_ff_2_q, j_k_ff_2_qn, j_k_ff_3_q, j_k_ff_3_qn, j_k_ff_4_q, n7_seg_driver_1_a,
       n7_seg_driver_1_b, n7_seg_driver_1_c, n7_seg_driver_1_d, n7_seg_driver_1_e, n7_seg_driver_1_f,
       n7_seg_driver_1_g, not_1_out, or_1_out, or_2_out, or_3_out;

  Clock clock_1 (.out(clock_1_out));
  not not_1 (not_1_out, in_1);
  J_K_Flip_Flop j_k_ff_1 (
    .J(1'b1), .clk(clock_1_out), .K(1'b1), .Q(j_k_ff_1_q), .Qn(j_k_ff_1_qn), .reset(and_7_out));  // open: preset, en
  and and_1 (and_1_out, not_1_out, j_k_ff_1_q);
  and and_2 (and_2_out, in_1, j_k_ff_1_qn);
  or or_1 (or_1_out, and_1_out, and_2_out);
  J_K_Flip_Flop j_k_ff_2 (
    .J(or_1_out), .clk(clock_1_out), .K(or_1_out), .Q(j_k_ff_2_q), .Qn(j_k_ff_2_qn), .reset(and_7_out));  // open: preset, en
  and and_3 (and_3_out, and_1_out, j_k_ff_2_q);
  and and_4 (and_4_out, j_k_ff_2_qn, and_2_out);
  or or_2 (or_2_out, and_3_out, and_4_out);
  _7_seg_Driver u_7_seg_driver_1 (
    .a(n7_seg_driver_1_a), .b(n7_seg_driver_1_b), .c(n7_seg_driver_1_c), .d(n7_seg_driver_1_d),
    .e(n7_seg_driver_1_e), .f(n7_seg_driver_1_f), .g(n7_seg_driver_1_g), .B0(j_k_ff_1_q), .B1(j_k_ff_2_q),
    .B2(j_k_ff_3_q), .B3(j_k_ff_4_q));
  J_K_Flip_Flop j_k_ff_3 (
    .J(or_2_out), .clk(clock_1_out), .K(or_2_out), .Q(j_k_ff_3_q), .Qn(j_k_ff_3_qn), .reset(and_7_out));  // open: preset, en
  _7_Segment_Display u_7_segment_display_1 (
    .g(n7_seg_driver_1_g), .f(n7_seg_driver_1_f), .a(n7_seg_driver_1_a), .b(n7_seg_driver_1_b),
    .e(n7_seg_driver_1_e), .d(n7_seg_driver_1_d), .c(n7_seg_driver_1_c));  // open: dp
  and and_5 (and_5_out, and_3_out, j_k_ff_3_q);
  and and_6 (and_6_out, j_k_ff_3_qn, and_4_out);
  J_K_Flip_Flop j_k_ff_4 (
    .J(or_3_out), .clk(clock_1_out), .K(or_3_out), .Q(j_k_ff_4_q), .reset(and_7_out));  // open: Qn, preset, en
  or or_3 (or_3_out, and_5_out, and_6_out);
  and and_7 (and_7_out, j_k_ff_4_q, j_k_ff_2_q);
endmodule
